// Logisim project alu_2bit.circ as structural Verilog: 6 circuits, main circuit divisor_1bit
module divisor_1bit (
  input  A,
  input  B,
  output C,
  output Y
);

  and and_1 (Y, A, B);

  assign C = 1'b0;
endmodule

module subtractor_1bit (
  input  A,
  input  B,
  output C,
  output Y
);

  wire and_2_out, and_3_out, not_1_out, not_2_out;

  not not_1 (not_1_out, B);
  not not_2 (not_2_out, A);
  and and_1 (C, not_2_out, B);
  and and_2 (and_2_out, A, not_1_out);
  and and_3 (and_3_out, not_2_out, B);
  or or_1 (Y, and_2_out, and_3_out);
endmodule

module adder_1bit (
  input  A,
  input  B,
  output C,
  output Y
);

  wire and_1_out, and_2_out, not_1_out, not_2_out;

  not not_1 (not_1_out, B);
  not not_2 (not_2_out, A);
  and and_1 (and_1_out, A, not_1_out);
  and and_2 (and_2_out, not_2_out, B);
  and and_3 (C, A, B);
  or or_1 (Y, and_1_out, and_2_out);
endmodule

module multiplier_1bit (
  input  A,
  input  B,
  output C,
  output Y
);

  and and_1 (Y, A, B);

  assign C = 1'b0;
endmodule

module alu (
  input  A,
  input  B,
  input  [1:0] Op,
  output C,
  output Y
);

  wire adder_1bit_1_c, adder_1bit_1_y, divisor_1bit_1_c, divisor_1bit_1_y, multiplier_1bit_1_c,
       multiplier_1bit_1_y, subtractor_1bit_1_c, subtractor_1bit_1_y;

  adder_1bit adder_1bit_1 (.A(A), .B(B), .C(adder_1bit_1_c), .Y(adder_1bit_1_y));
  subtractor_1bit subtractor_1bit_1 (.A(A), .B(B), .C(subtractor_1bit_1_c), .Y(subtractor_1bit_1_y));
  multiplier_1bit multiplier_1bit_1 (.A(A), .B(B), .C(multiplier_1bit_1_c), .Y(multiplier_1bit_1_y));
  divisor_1bit divisor_1bit_1 (.A(A), .B(B), .C(divisor_1bit_1_c), .Y(divisor_1bit_1_y));
  Multiplexer #(.select(2)) multiplexer_1 (
    .in0(adder_1bit_1_c), .in1(subtractor_1bit_1_c), .in2(multiplier_1bit_1_c), .in3(divisor_1bit_1_c),
    .out(C), .sel(Op));
  Multiplexer #(.select(2)) multiplexer_2 (
    .in0(adder_1bit_1_y), .in1(subtractor_1bit_1_y), .in2(multiplier_1bit_1_y), .in3(divisor_1bit_1_y),
    .out(Y), .sel(Op));
endmodule

module main (
  input  in_1,
  input  in_2,
  input  [1:0] in_3,
  output C,
  output Y
);

  alu alu_1 (.A(in_1), .B(in_2), .Op(in_3), .C(C), .Y(Y));
endmodule
