// Logisim project alu_ic_74181.circ as structural Verilog: 1 circuit, main circuit main
module main (
  input  [3:0] OP,
  input  [3:0] A,
  input  [3:0] B,
  input  M,
  output [3:0] Y
);

  // _74181 #(.ShowInternalStructure("true"), .VccGndPorts("true")) 74181_1: pin names not known; wires that end beside it: 1'b0, Y[3], Y[2], Y[1], Y[0], M, B[3], OP[0], A[3], OP[1], B[2], OP[2], A[2], OP[3], B[1], A[0], A[1], B[0], 1'b1
endmodule
