// Logisim project my_2bit_alu.circ as structural Verilog: 1 circuit, main circuit main
module main (
);

  wire adder_1_cout, clock_1_out, comparator_1_eq, decoder_1_out0, decoder_1_out1, multiplexer_2_out,
       subtractor_1_bout;
  wire [3:0] IR_q_3, multiplexer_1_out, multiplexer_1_out_2, ROP_q;
  wire [7:0] adder_1_out, and_1_out, Counter_q, divider_1_out, IR_q, multiplier_1_out, or_1_out, RA_q, RB_q,
       shifter_1_out, shifter_2_out, subtractor_1_out;
  wire [11:8] IR_q_2;
  wire [15:0] rom_1_data;

  Decoder #(.select(4), .enable("false")) decoder_1 (
    .out0(decoder_1_out0), .out1(decoder_1_out1), .sel(IR_q_3));  // open: out2, out3, out4, out5, out6, out7, out8, out9, out10, out11, out12, out13, out14, out15
  Clock clock_1 (.out(clock_1_out));
  Counter Counter (.Q(Counter_q), .clk(clock_1_out));  // open: load, D, count, carry, clr
  ROM #(.dataWidth(16)) rom_1 (.addr(Counter_q), .data(rom_1_data));  // open: sel
  Register RA (.D(IR_q), .en(decoder_1_out0), .Q(RA_q), .clk(clock_1_out));  // open: clr
  Register RB (.D(IR_q), .en(decoder_1_out1), .Q(RB_q), .clk(clock_1_out));  // open: clr
  Register #(.width(16)) IR (.D(rom_1_data), .Q({IR_q_3, IR_q_2, IR_q}), .clk(clock_1_out));  // open: en, clr
  LED led_1 (.in(clock_1_out));
  Register #(.width(4)) ROP (.D(IR_q_2), .Q(ROP_q));  // open: en, clk, clr
  Adder adder_1 (.a(RA_q), .b(RB_q), .out(adder_1_out), .cout(adder_1_cout));  // open: cin
  Subtractor subtractor_1 (.a(RA_q), .b(RB_q), .out(subtractor_1_out), .bout(subtractor_1_bout));  // open: bin
  Multiplier multiplier_1 (.a(RA_q), .b(RB_q), .out(multiplier_1_out));  // open: cin, cout
  Divider divider_1 (.a(RA_q), .b(RB_q), .out(divider_1_out));  // open: upper, rem
  assign and_1_out = RA_q & RB_q;  // AND_Gate and_1, 8 bits wide
  assign or_1_out = RA_q | RB_q;  // OR_Gate or_1, 8 bits wide
  Shifter shifter_1 (.in(RA_q), .\dist (RB_q[2:0]), .out(shifter_1_out));
  Shifter shifter_2 (.in(RA_q), .\dist (RB_q[2:0]), .out(shifter_2_out));
  Multiplexer #(.select(4), .width(8), .enable("false")) multiplexer_1 (
    .in0(adder_1_out), .in1(subtractor_1_out), .in2(multiplier_1_out), .in3(divider_1_out), .in4(and_1_out),
    .in5(or_1_out), .in6(shifter_1_out), .in7(shifter_2_out), .in8({8{1'b0}}), .in9({8{1'b0}}),
    .in10({8{1'b0}}), .in11({8{1'b0}}), .in12({8{1'b0}}), .in13({8{1'b0}}), .in14({8{1'b0}}),
    .in15({8{1'b0}}), .out({multiplexer_1_out_2, multiplexer_1_out}), .sel(ROP_q));
  Hex_Digit_Display hex_digit_display_1 (.value(multiplexer_1_out_2));  // open: dp
  // Probe on {multiplexer_1_out_2, multiplexer_1_out}
  Comparator comparator_1 (
    .a({multiplexer_1_out_2, multiplexer_1_out}), .b({8{1'b0}}), .eq(comparator_1_eq));  // open: gt, lt
  Multiplexer #(.select(4), .enable("false")) multiplexer_2 (
    .in0(adder_1_cout), .in1(subtractor_1_bout), .in2(1'b0), .in3(1'b0), .in4(1'b0), .in5(1'b0), .in6(1'b0),
    .in7(1'b0), .in8(1'b0), .in9(1'b0), .in10(1'b0), .in11(1'b0), .in12(1'b0), .in13(1'b0), .in14(1'b0),
    .in15(1'b0), .out(multiplexer_2_out), .sel(ROP_q));
  Hex_Digit_Display hex_digit_display_2 (.value(multiplexer_1_out));  // open: dp
  // Probe on comparator_1_eq
  LED led_2 (.in(comparator_1_eq));
  // Probe on multiplexer_2_out
  LED led_3 (.in(multiplexer_2_out));

  // Notes on the sheet:
  //   contents of rom_1 (hex, n*v repeats v):
  //   1000 2001 1000 2002 1000 2003 1000 2004 1000 2005 1000 2006 1000 2007 1000 2008 1000 2009 1000 200a
  //   1000
endmodule
